# Fritzing sketch ESP8266_Arduino (saved by Fritzing 0.9.3b)
circuit board: 8.46667cm x 5.64444cm
perfboards: 1

parts:
  IC1 = Voltage Regulator [package=to-220-alt]
  R1 = Resistor [tolerance=±5% resistance=1k package=THT]
  R2 = Resistor [tolerance=±10% resistance=2k package=THT]
  R3 = Resistor [tolerance=±5% resistance=10k package=THT]
  U1 = ESP8266 WiFi Module [part_number=ESP8266]
  J1 = female pin header, 4 pins [form="♀ (female)"]
  C3 = Capacitor Polarized [package=panasonic_g]
  C4 = Capacitor [package=cap-pth-small2]

nets:
  GND: IC1.GND, R2.Pin_0, U1.GND, J1.pin4, C3.-, C4.1
  N1: IC1.IN, J1.pin3
  N2: IC1.OUT, R3.Pin_0, U1.VCC, C3.+, C4.2
  N3: R1.Pin_0, J1.pin1
  N4: R1.Pin_1, R2.Pin_1, U1.RXD
  N5: R3.Pin_1, U1.CH_PD
  N6: U1.TXD, J1.pin2

custom parts:
  ESP8266 WiFi Module: Generic WiFi Module based on the ESP8266 with onboard PCB antenna and UART communications
